# Fritzing sketch arduino car (saved by Fritzing 0.9.10b)

parts:
  Part1 = Arduino Uno (Rev3) - ICSP
  U1 = Voltage Regulator - 5V [package="DPak [SMD]"]
  C1 = Capacitor [package=cap-pth-small2]
  L298N1 = L298N DC motor driver
  M1 = gear-motor
  U2 = ESP8266 WiFi Module [part_number=ESP8266]
  Part2 = Bluetooth HC-05 Macho
  Part3 = Black Joystick KY-023
  Mod1 = KY-022 Infrared Receiver Module [package="Breakout board"]
  C2 = Capacitor [package=cap-pth-small2]
  M2 = gear-motor  # not connected
  M3 = gear-motor  # not connected
  M4 = gear-motor
  VCC1 = 4 x AAA Battery Mount
  S1 = Toggle Switch spst [package=THT]

nets:
  N1: Part1.A4/SDA, Part3.VRy
  N2: Part1.A5/SCL, Part3.VRx
  N3: Part1.D8, L298N1.IN2
  N4: Part1.D9_PWM, L298N1.ENA
  N5: Part1.D10_PWM/SS, L298N1.ENB
  N6: Part1.D11_PWM/MOSI, L298N1.IN3
  N7: Part1.D12/MISO, L298N1.IN4
  GND: Part1.GND, U1.GND, C1.1, L298N1.GND, U2.GND, Part3.GND, C2.2, VCC1.-
  N8: Part1.D2, U2.RXD
  N9: Part1.D3_PWM, U2.TXD
  N10: Part1.D4, Part2.RXD
  N11: Part1.D5_PWM, Part2.TXD
  N12: Part1.D6_PWM, Mod1.S
  N13: Part1.D7, L298N1.IN1
  3V3: Part1.3V3, U2.VCC
  5V: Part1.5V, Mod1.Vin
  VIN: Part1.VIN, U1.output_voltage, C1.2, L298N1.12V
  N14: U1.input_voltage, S1.COM
  N15: L298N1.OUT1, M4.pin_2
  N16: L298N1.OUT2, M4.pin_1
  N17: L298N1.OUT3, M1.pin_1
  N18: L298N1.OUT4, M1.pin_2

custom parts:
  L298N DC motor driver: 2x DC motor driver with 78M05 positive voltage regulator (7..35 V) L298N: max 46 V, 2 A Set 5 V Enable jumper to enable 5 V regultor (needed for the L298N) and +5 V output at screw terminal or supply external +5 V at screw terminal Set ENA and/or ENB to +5 V to enable motor permanently or supply ENA and/or ENB with PWM signal IN1 and IN2 set rotation directory for motor A (OUT1/OUT2) IN2 and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
  ESP8266 WiFi Module: Generic WiFi Module based on the ESP8266 with onboard PCB antenna and UART communications
  Black Joystick KY-023: Description: The joystick is a combination of 2 analoog potentiometer and a digital switch. Arduino GND --> Module pin - Arduino +5V --> Module pin +5V Arduino Analoog 0 --> Module VRx Arduino Analoog 1 --> Module VRy Arduino Digital --> Module SW Dimensions: 1" x 1.25"
  KY-022 Infrared Receiver Module: KY-022 IR receiver module, reacts to 38kHz infrared light.
  Toggle Switch spst: Toggle Switch single pole single throw
