# Fritzing sketch esp car (saved by Fritzing 0.9.10b)

parts:
  L298N1 = L298N DC motor driver
  M1 = gear-motor
  M2 = gear-motor  # not connected
  M3 = gear-motor  # not connected
  M4 = gear-motor
  S1 = Toggle Switch spst [package=THT]
  MH-ET_LIVE_ESP32_DEVKIT1 = MH-ET LIVE ESP32 DEVKIT 38 pins
  Part4 = NRF24L01+ Breakout Board
  Mod1 = KY-022 Infrared Receiver Module [package="Breakout board"]
  VCC1 = 4 x AAA Battery Mount

nets:
  N1: L298N1.OUT1, M4.pin_2
  N2: L298N1.OUT2, M4.pin_1
  N3: L298N1.OUT3, M1.pin_1
  N4: L298N1.OUT4, M1.pin_2
  N5: L298N1.12V, S1.L1
  GND: L298N1.GND, MH-ET_LIVE_ESP32_DEVKIT1.CMD, Part4.GND, Mod1.-, VCC1.-
  5V: L298N1.5V, MH-ET_LIVE_ESP32_DEVKIT1.5V, Part4.VCC, Mod1.Vin
  N6: L298N1.ENA, MH-ET_LIVE_ESP32_DEVKIT1.IO25
  N7: L298N1.ENB, MH-ET_LIVE_ESP32_DEVKIT1.IO12
  N8: L298N1.IN1, MH-ET_LIVE_ESP32_DEVKIT1.IO26
  N9: L298N1.IN2, MH-ET_LIVE_ESP32_DEVKIT1.IO27
  N10: L298N1.IN3, MH-ET_LIVE_ESP32_DEVKIT1.IO13
  N11: L298N1.IN4, MH-ET_LIVE_ESP32_DEVKIT1.IO14
  N12: S1.COM, VCC1.+
  N13: MH-ET_LIVE_ESP32_DEVKIT1.IO23, Part4.MOSI
  N14: MH-ET_LIVE_ESP32_DEVKIT1.IO22, Mod1.S
  N15: MH-ET_LIVE_ESP32_DEVKIT1.IO19, Part4.MISO
  N16: MH-ET_LIVE_ESP32_DEVKIT1.IO18, Part4.SCK
  N17: MH-ET_LIVE_ESP32_DEVKIT1.IO17, Part4.CS
  N18: MH-ET_LIVE_ESP32_DEVKIT1.IO16, Part4.CE

custom parts:
  L298N DC motor driver: 2x DC motor driver with 78M05 positive voltage regulator (7..35 V) L298N: max 46 V, 2 A Set 5 V Enable jumper to enable 5 V regultor (needed for the L298N) and +5 V output at screw terminal or supply external +5 V at screw terminal Set ENA and/or ENB to +5 V to enable motor permanently or supply ENA and/or ENB with PWM signal IN1 and IN2 set rotation directory for motor A (OUT1/OUT2) IN2 and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
  Toggle Switch spst: Toggle Switch single pole single throw
  MH-ET LIVE ESP32 DEVKIT 38 pins: http://mh.nodebb.com/topic/2/mh-et-live-esp32-devkit
  KY-022 Infrared Receiver Module: KY-022 IR receiver module, reacts to 38kHz infrared light.
