# Fritzing sketch remote (saved by Fritzing 0.9.10b)

parts:
  Part1 = Black Joystick KY-023
  Part2 = Black Joystick KY-023
  Part3 = Arduino Nano (Rev3.0) (ICSP)
  Part4 = NRF24L01+ Breakout Board
  VCC3 = Battery
  S2 = Toggle Switch spst [package=THT]

nets:
  N1: Part1.VRy, Part3.A1
  N2: Part1.VRx, Part3.A0
  +5V: Part1.+5V, Part2.+5V, Part3.5V, Part4.VCC
  GND: Part1.GND, Part2.GND, Part3.GND, Part4.GND, VCC3.-
  N3: Part2.VRy, Part3.A3
  N4: Part2.VRx, Part3.A2
  N5: Part3.D7, Part4.CE
  N6: Part3.D8, Part4.CS
  N7: Part3.D11/MOSI, Part4.MOSI
  N8: Part3.D12/MISO, Part4.MISO
  N9: Part3.VIN, S2.L1
  N10: Part3.D13/SCK, Part4.SCK
  N11: VCC3.+, S2.COM

custom parts:
  Black Joystick KY-023: Description: The joystick is a combination of 2 analoog potentiometer and a digital switch. Arduino GND --> Module pin - Arduino +5V --> Module pin +5V Arduino Analoog 0 --> Module VRx Arduino Analoog 1 --> Module VRy Arduino Digital --> Module SW Dimensions: 1" x 1.25"
  Toggle Switch spst: Toggle Switch single pole single throw
